# Fritzing sketch 布线图 (saved by Fritzing 0.9.3b)

parts:
  元件1 = Arduino Mega 2560 (Rev3)
  Adafruit_HUZZAH_ESP8266_Breakout1 = Adafruit HUZZAH ESP8266 Breakout [part_number=2471]
  J1 = Basic Servo
  J2 = Basic Servo
  J4 = Basic Servo
  J5 = Basic Servo
  VCC1 = Battery block 9V
  J6 = Basic Servo
  J7 = Basic Servo
  J8 = Basic Servo
  J9 = Basic Servo
  M1 = DC Motor  # not connected
  M2 = DC Motor  # not connected
  M3 = Stepper Motor - Unipolar

nets:
  GND: 元件1.GND, Adafruit_HUZZAH_ESP8266_Breakout1.GND, J1.gnd, J2.gnd, J4.gnd, J5.gnd, VCC1.-, J7.gnd, J8.gnd, J9.gnd, M3.C
  N1: 元件1.D13_PWM, M3.COMMON_1
  N2: 元件1.D12_PWM, M3.COMMON_2
  N3: 元件1.5V, Adafruit_HUZZAH_ESP8266_Breakout1.V+
  VCC: 元件1.VIN, VCC1.+, J7.vcc, J8.vcc, J9.vcc, M3.A
  N4: 元件1.D28, Adafruit_HUZZAH_ESP8266_Breakout1.RX
  N5: 元件1.D29, Adafruit_HUZZAH_ESP8266_Breakout1.TX
  N6: 元件1.D40, J6.pulse, J8.pulse
  N7: 元件1.D41, J9.pulse
  N8: 元件1.D43, J7.pulse
  N9: 元件1.D44, J1.pulse
  N10: 元件1.D45, J4.pulse
  N11: 元件1.D46, J2.pulse
  N12: 元件1.D47, J5.pulse
